# Fritzing sketch MEM_prototype (saved by Fritzing 0.9.3b)
circuit board: 4.5cm x 3cm
breadboards: 1

parts:
  J2 = female pin header, 6 pins [form="♀ (female)"]
  IC1 = SO08 [chip_label=IC part_number="W25Q64JVSSIQ (8MB FLASH)" package=SO]
  IC2 = SO08 [chip_label=IC part_number="25LC256 (32kB EEPROM)" package=SO]
  IC3 = SO08 [chip_label=IC part_number="25LC640 (8kB EEPROM)" package=SO]
  IC4 = Voltage Regulator LM1117 [part_number=AMS1117 package=sot223]
  J1 = female pin header, 6 pins [form="♀ (female)"]
  R1 = Resistor [tolerance=±5% resistance=1k package="1206 [SMD]"]
  R2 = Resistor [tolerance=±5% resistance=2k package="1206 [SMD]"]
  R3 = Resistor [tolerance=±5% resistance=1k package="1206 [SMD]"]
  R4 = Resistor [tolerance=±5% resistance=2k package="1206 [SMD]"]
  LED1 = smd LED [color="Red (633nm)" package="1206 [SMD]"]
  R5 = Resistor [tolerance=±5% resistance=2k package="1206 [SMD]"]

nets:
  NCS0: J2.pin1, R1.Pin_0
  NCS1: J2.pin2, IC2.1
  NCS2: J2.pin3, IC3.1
  NRST0: J2.pin4, R3.Pin_0
  NRST1: J2.pin5, IC2.7
  NRST2: J2.pin6, IC3.7
  NCS0V3: IC1.1, R1.Pin_1, R2.Pin_0
  MISO: IC1.2, IC2.2, IC3.2, J1.pin3
  3V3: IC1.3, IC1.8, IC4.OUT
  GND: IC1.4, IC2.4, IC3.4, IC4.ADJ, J1.pin5, J1.pin6, R2.Pin_1, R4.Pin_1, R5.Pin_1
  MOSI: IC1.5, IC2.5, IC3.5, J1.pin2
  SCK: IC1.6, IC2.6, IC3.6, J1.pin4
  NRST0V3: IC1.7, R3.Pin_1, R4.Pin_0
  5V: IC2.3, IC2.8, IC3.3, IC3.8, IC4.IN, J1.pin1, LED1.anode
  N1: LED1.cathode, R5.Pin_0

notes:
  MEM01A1
  Memory Modul
  © Ahmed Ibrahim Gazar
  2024-12-04
  MEM01A1, MEM01A1 - Memory Module Circuit Design, A1
