# Fritzing sketch PSU_prototype (saved by Fritzing 0.9.3b)
circuit board: 10cm x 8cm
breadboards: 1

parts:
  J1 = female pin header, 4 pins [form="♀ (female)"]
  J2 = female pin header, 4 pins [form="♀ (female)"]
  Q1 = NPN-Transistor [part_number=2N3904 package="TO92 [THT]"]
  Q2 = PNP-Transistor [part_number=2N3906 package="TO92 [THT]"]
  Q3 = NPN-Transistor [part_number=2N3904 package="TO92 [THT]"]
  Q4 = PNP-Transistor [part_number=2N3906 package="TO92 [THT]"]
  Q5 = NPN-Transistor [part_number=2N3904 package="TO92 [THT]"]
  Q6 = PNP-Transistor [part_number=2N3906 package="TO92 [THT]"]
  Q7 = NPN-Transistor [part_number=2N3904 package="TO92 [THT]"]
  Q8 = PNP-Transistor [part_number=2N3906 package="TO92 [THT]"]
  J3 = female pin header, 16 pins [form="♀ (female)"]
  Q9 = NPN-Transistor [part_number=2N3904 package="TO92 [THT]"]
  Q11 = NPN-Transistor [part_number=2N3904 package="TO92 [THT]"]
  Q12 = NPN-Transistor [part_number=2N3904 package="TO92 [THT]"]
  Q13 = PNP-Transistor [part_number=2N3906 package="TO92 [THT]"]
  Q14 = PNP-Transistor [part_number=2N3906 package="TO92 [THT]"]
  Q15 = PNP-Transistor [part_number=2N3906 package="TO92 [THT]"]
  Q16 = PNP-Transistor [part_number=2N3906 package="TO92 [THT]"]
  Q17 = NPN-Transistor [part_number=2N3904 package="TO92 [THT]"]
  Q18 = NPN-Transistor [part_number=2N3904 package="TO92 [THT]"]
  Q19 = NPN-Transistor [part_number=2N3904 package="TO92 [THT]"]
  Q20 = NPN-Transistor [part_number=2N3904 package="TO92 [THT]"]
  Q21 = NPN-Transistor [part_number=2N3904 package="TO92 [THT]"]
  Q22 = NPN-Transistor [part_number=2N3904 package="TO92 [THT]"]
  Q23 = NPN-Transistor [part_number=2N3904 package="TO92 [THT]"]
  Q24 = NPN-Transistor [part_number=2N3904 package="TO92 [THT]"]
  Q25 = PNP-Transistor [part_number=2N3906 package="TO92 [THT]"]
  Q26 = PNP-Transistor [part_number=2N3906 package="TO92 [THT]"]
  Q27 = PNP-Transistor [part_number=2N3906 package="TO92 [THT]"]
  Q28 = PNP-Transistor [part_number=2N3906 package="TO92 [THT]"]
  Q29 = PNP-Transistor [part_number=2N3906 package="TO92 [THT]"]
  Q30 = PNP-Transistor [part_number=2N3906 package="TO92 [THT]"]
  Q31 = PNP-Transistor [part_number=2N3906 package="TO92 [THT]"]
  Q32 = PNP-Transistor [part_number=2N3906 package="TO92 [THT]"]
  Q10 = NPN-Transistor [part_number=2N3904 package="TO92 [THT]"]
  IC1 = SO-28W [chip_label=IC part_number=MCP23017 package=SO(w)]
  R25 = Resistor [tolerance=±5% resistance=10k package="1206 [SMD]"]
  R13 = Resistor [tolerance=±5% resistance=10k package="1206 [SMD]"]
  R26 = Resistor [tolerance=±5% resistance=10k package="1206 [SMD]"]
  R10 = Resistor [tolerance=±5% resistance=10k package="1206 [SMD]"]
  R27 = Resistor [tolerance=±5% resistance=10k package="1206 [SMD]"]
  R14 = Resistor [tolerance=±5% resistance=10k package="1206 [SMD]"]
  R28 = Resistor [tolerance=±5% resistance=10k package="1206 [SMD]"]
  R7 = Resistor [tolerance=±5% resistance=10k package="1206 [SMD]"]
  R29 = Resistor [tolerance=±5% resistance=10k package="1206 [SMD]"]
  R15 = Resistor [tolerance=±5% resistance=10k package="1206 [SMD]"]
  R30 = Resistor [tolerance=±5% resistance=10k package="1206 [SMD]"]
  R4 = Resistor [tolerance=±5% resistance=10k package="1206 [SMD]"]
  R31 = Resistor [tolerance=±5% resistance=10k package="1206 [SMD]"]
  R16 = Resistor [tolerance=±5% resistance=10k package="1206 [SMD]"]
  R32 = Resistor [tolerance=±5% resistance=10k package="1206 [SMD]"]
  R3 = Resistor [tolerance=±5% resistance=10k package="1206 [SMD]"]
  R41 = Resistor [tolerance=±5% resistance=10k package="1206 [SMD]"]
  R21 = Resistor [tolerance=±5% resistance=10k package="1206 [SMD]"]
  R42 = Resistor [tolerance=±5% resistance=10k package="1206 [SMD]"]
  R12 = Resistor [tolerance=±5% resistance=10k package="1206 [SMD]"]
  R43 = Resistor [tolerance=±5% resistance=10k package="1206 [SMD]"]
  R22 = Resistor [tolerance=±5% resistance=10k package="1206 [SMD]"]
  R44 = Resistor [tolerance=±5% resistance=10k package="1206 [SMD]"]
  R9 = Resistor [tolerance=±5% resistance=10k package="1206 [SMD]"]
  R45 = Resistor [tolerance=±5% resistance=10k package="1206 [SMD]"]
  R23 = Resistor [tolerance=±5% resistance=10k package="1206 [SMD]"]
  R46 = Resistor [tolerance=±5% resistance=10k package="1206 [SMD]"]
  R6 = Resistor [tolerance=±5% resistance=10k package="1206 [SMD]"]
  R47 = Resistor [tolerance=±5% resistance=10k package="1206 [SMD]"]
  R24 = Resistor [tolerance=±5% resistance=10k package="1206 [SMD]"]
  R48 = Resistor [tolerance=±5% resistance=10k package="1206 [SMD]"]
  R1 = Resistor [tolerance=±5% resistance=10k package="1206 [SMD]"]
  R33 = Resistor [tolerance=±5% resistance=100k package="1206 [SMD]"]
  R17 = Resistor [tolerance=±5% resistance=100k package="1206 [SMD]"]
  R34 = Resistor [tolerance=±5% resistance=100k package="1206 [SMD]"]
  R11 = Resistor [tolerance=±5% resistance=100k package="1206 [SMD]"]
  R35 = Resistor [tolerance=±5% resistance=100k package="1206 [SMD]"]
  R18 = Resistor [tolerance=±5% resistance=100k package="1206 [SMD]"]
  R36 = Resistor [tolerance=±5% resistance=100k package="1206 [SMD]"]
  R8 = Resistor [tolerance=±5% resistance=100k package="1206 [SMD]"]
  R37 = Resistor [tolerance=±5% resistance=100k package="1206 [SMD]"]
  R19 = Resistor [tolerance=±5% resistance=100k package="1206 [SMD]"]
  R38 = Resistor [tolerance=±5% resistance=100k package="1206 [SMD]"]
  R5 = Resistor [tolerance=±5% resistance=100k package="1206 [SMD]"]
  R39 = Resistor [tolerance=±5% resistance=100k package="1206 [SMD]"]
  R20 = Resistor [tolerance=±5% resistance=100k package="1206 [SMD]"]
  R40 = Resistor [tolerance=±5% resistance=100k package="1206 [SMD]"]
  R2 = Resistor [tolerance=±5% resistance=100k package="1206 [SMD]"]
  PWR_LED = smd LED [color="Green (565nm)" package="1206 [SMD]"]
  R49 = Resistor [tolerance=±5% resistance=1k package="1206 [SMD]"]

nets:
  VCC: J1.pin1, Q2.E, Q4.E, Q6.E, Q8.E, Q13.E, Q14.E, Q15.E, Q16.E, Q25.E, Q26.E, Q27.E, Q28.E, Q29.E, Q30.E, Q31.E, Q32.E, IC1.9, R33.Pin_0, R17.Pin_0, R34.Pin_0, R11.Pin_0, R35.Pin_0, R18.Pin_0, R36.Pin_0, R8.Pin_0, R37.Pin_0, R19.Pin_0, R38.Pin_0, R5.Pin_0, R39.Pin_0, R20.Pin_0, R40.Pin_0, R2.Pin_0, PWR_LED.anode
  I2C_SDA: J1.pin2, IC1.13
  I2C_SCL: J1.pin3, IC1.12
  GND: J1.pin4, Q1.E, Q3.E, Q5.E, Q7.E, Q9.E, Q11.E, Q12.E, Q17.E, Q18.E, Q19.E, Q20.E, Q21.E, Q22.E, Q23.E, Q24.E, Q10.E, IC1.10, R49.Pin_1
  NRST: J2.pin1, IC1.18
  A2: J2.pin2, IC1.17
  A1: J2.pin3, IC1.16
  A0: J2.pin4, IC1.15
  N1: Q1.B, R1.Pin_1
  N2: Q1.C, R3.Pin_0, R2.Pin_1
  N3: Q2.B, R3.Pin_1
  PWR_OUT.0: Q2.C, J3.pin1
  N4: Q3.B, R6.Pin_1
  N5: Q3.C, R4.Pin_0, R5.Pin_1
  N6: Q4.B, R4.Pin_1
  PWR_OUT.1: Q4.C, J3.pin2
  N7: Q5.B, R9.Pin_1
  N8: Q5.C, R7.Pin_0, R8.Pin_1
  N9: Q6.B, R7.Pin_1
  PWR_OUT.2: Q6.C, J3.pin3
  N10: Q7.B, R12.Pin_1
  N11: Q7.C, R10.Pin_0, R11.Pin_1
  N12: Q8.B, R10.Pin_1
  PWR_OUT.3: Q8.C, J3.pin4
  PWR_OUT.4: J3.pin5, Q16.C
  PWR_OUT.5: J3.pin6, Q15.C
  PWR_OUT.6: J3.pin7, Q14.C
  PWR_OUT.7: J3.pin8, Q13.C
  PWR_OUT.8: J3.pin9, Q32.C
  PWR_OUT.9: J3.pin10, Q30.C
  PWR_OUT.10: J3.pin11, Q28.C
  PWR_OUT.11: J3.pin12, Q26.C
  PWR_OUT.12: J3.pin13, Q31.C
  PWR_OUT.13: J3.pin14, Q29.C
  PWR_OUT.14: J3.pin15, Q27.C
  PWR_OUT.15: J3.pin16, Q25.C
  N13: Q9.B, R21.Pin_1
  N14: Q9.C, R13.Pin_0, R17.Pin_1
  N15: Q11.B, R23.Pin_1
  N16: Q11.C, R15.Pin_0, R19.Pin_1
  N17: Q12.B, R24.Pin_1
  N18: Q12.C, R16.Pin_0, R20.Pin_1
  N19: Q13.B, R13.Pin_1
  N20: Q14.B, R14.Pin_1
  N21: Q15.B, R15.Pin_1
  N22: Q16.B, R16.Pin_1
  N23: Q17.B, R41.Pin_1
  N24: Q17.C, R25.Pin_0, R33.Pin_1
  N25: Q18.B, R42.Pin_1
  N26: Q18.C, R26.Pin_0, R34.Pin_1
  N27: Q19.B, R43.Pin_1
  N28: Q19.C, R27.Pin_0, R35.Pin_1
  N29: Q20.B, R44.Pin_1
  N30: Q20.C, R28.Pin_0, R36.Pin_1
  N31: Q21.B, R45.Pin_1
  N32: Q21.C, R29.Pin_0, R37.Pin_1
  N33: Q22.B, R46.Pin_1
  N34: Q22.C, R30.Pin_0, R38.Pin_1
  N35: Q23.B, R47.Pin_1
  N36: Q23.C, R31.Pin_0, R39.Pin_1
  N37: Q24.B, R48.Pin_1
  N38: Q24.C, R32.Pin_0, R40.Pin_1
  N39: Q25.B, R25.Pin_1
  N40: Q26.B, R26.Pin_1
  N41: Q27.B, R27.Pin_1
  N42: Q28.B, R28.Pin_1
  N43: Q29.B, R29.Pin_1
  N44: Q30.B, R30.Pin_1
  N45: Q31.B, R31.Pin_1
  N46: Q32.B, R32.Pin_1
  N47: Q10.B, R22.Pin_1
  N48: Q10.C, R14.Pin_0, R18.Pin_1
  PWR_EN.0: IC1.1, R1.Pin_0
  PWR_EN.1: IC1.2, R6.Pin_0
  PWR_EN.2: IC1.3, R9.Pin_0
  PWR_EN.3: IC1.4, R12.Pin_0
  PWR_EN.4: IC1.5, R24.Pin_0
  PWR_EN.5: IC1.6, R23.Pin_0
  PWR_EN.6: IC1.7, R22.Pin_0
  PWR_EN.7: IC1.8, R21.Pin_0
  PWR_EN.15: IC1.21, R41.Pin_0
  PWR_EN.14: IC1.22, R43.Pin_0
  PWR_EN.13: IC1.23, R45.Pin_0
  PWR_EN.12: IC1.24, R47.Pin_0
  PWR_EN.11: IC1.25, R42.Pin_0
  PWR_EN.10: IC1.26, R44.Pin_0
  PWR_EN.9: IC1.27, R46.Pin_0
  PWR_EN.8: IC1.28, R48.Pin_0
  N49: PWR_LED.cathode, R49.Pin_0

notes:
  PSU01A1
  Power Switch Unit
  © Ahmed Ibrahim Gazar
  2024-12-03
  PSU01A1, PSU01A1 - Power Switch Unit Circuit Design, A1
