# Fritzing sketch PSM_prototype (saved by Fritzing 0.9.3b)
circuit board: 5cm x 2.5cm
breadboards: 1

parts:
  Q3 = PNP-Transistor [part_number=BC369 package="TO92 [THT]"]
  D4 = Zener Diode [part_number=ZY5.6 breakdown_voltage=5.1V package="300 mil [THT]"]
  R1 = Resistor [tolerance=±5% resistance=220 package="1206 [SMD]"]
  LED1 = smd LED [color="Red (633nm)" package="1206 [SMD]"]
  LED2 = smd LED [color="Red (633nm)" package="1206 [SMD]"]
  LED3 = smd LED [color="Red (633nm)" package="1206 [SMD]"]
  D3 = Rectifier Diode [part_number=1N4001 package="300 mil [THT]"]
  R6 = Resistor [tolerance=±5% resistance=220 package="1206 [SMD]"]
  R5 = Resistor [tolerance=±5% resistance=470 package="1206 [SMD]"]
  R4 = Resistor [tolerance=±5% resistance=6.8k package="1206 [SMD]"]
  R3 = Resistor [tolerance=±5% resistance=2.7k package="1206 [SMD]"]
  R2 = Resistor [tolerance=±5% resistance=220 package="1206 [SMD]"]
  X2 = USB Connectors [package=usb-mb-h]
  F1 = Resettable Fuse PTC [part_number=RKP-SMDB050 package=ptc-1206]
  J1 = male pin header, 4 pins [form="♂ (male)"]
  J2 = male pin header, 4 pins [form="♂ (male)"]
  Q4 = PNP-Transistor [part_number=BC369 package="TO92 [THT]"]

nets:
  U5V_FUSED: Q3.E, LED1.cathode, D3.cathode, R3.Pin_0, F1.2, Q4.E
  N1: Q3.B, R4.Pin_1
  N2: Q3.C, R5.Pin_0, Q4.B
  N3: D4.cathode, R4.Pin_0, R3.Pin_1, R2.Pin_1
  GND: D4.anode, D3.anode, R6.Pin_1, R5.Pin_1, X2.D+, J1.pin1, J1.pin2, J1.pin3, J1.pin4
  U5V: R1.Pin_0, X2.VBUS, F1.1
  N4: R1.Pin_1, LED1.anode
  U5V_REG: LED2.cathode, LED3.anode, J2.pin1, J2.pin2, J2.pin3, J2.pin4, Q4.C
  N5: LED2.anode, R2.Pin_0
  N6: LED3.cathode, R6.Pin_0

notes:
  PSM01A1
  Power Supply Module
  © Ahmed Ibrahim Gazar
  2024-12-10
  PSM01A1, PSM01A1 - Power Supply Module Circuit Design, A1
